# Fritzing sketch keyboard (saved by Fritzing 1.0.6)
breadboards: 3

parts:
  S6 = Pushbutton [package="[THT]"]
  S5 = Pushbutton [package="[THT]"]
  S4 = Pushbutton [package="[THT]"]
  S1 = Pushbutton [package="[THT]"]
  S2 = Pushbutton [package="[THT]"]
  S3 = Pushbutton [package="[THT]"]
  D3 = Rectifier Diode [part_number=1N4148 package="300 mil [THT]"]
  D4 = Rectifier Diode [part_number=1N4148 package="300 mil [THT]"]
  D5 = Rectifier Diode [part_number=1N4148 package="300 mil [THT]"]
  D6 = Rectifier Diode [part_number=1N4148 package="300 mil [THT]"]
  D7 = Rectifier Diode [part_number=1N4148 package="300 mil [THT]"]
  D8 = Rectifier Diode [part_number=1N4148 package="300 mil [THT]"]
  R2 = Resistor [tolerance=±5% power=0.25W resistance=220 package=THT]
  R3 = Resistor [tolerance=±5% power=0.25W resistance=220 package=THT]
  Part1 = Thumb Joystick
  XIAO_ESP32S3 = XIAO ESP32S3 [package="DIP (Dual Inline) [THT]"]
  RE1 = Rotary Encoder [package=THT]

nets:
  N1: S6.Pin_1, S6.Pin_2, S3.Pin_1, S3.Pin_2, XIAO_ESP32S3.D2
  N2: S6.Pin_3, S6.Pin_4, D8.anode
  N3: S5.Pin_1, S5.Pin_2, S2.Pin_1, S2.Pin_2, XIAO_ESP32S3.D4
  N4: S5.Pin_3, S5.Pin_4, D6.anode
  N5: S4.Pin_1, S4.Pin_2, S1.Pin_1, S1.Pin_2, XIAO_ESP32S3.D5
  N6: S4.Pin_3, S4.Pin_4, D5.anode
  N7: S1.Pin_3, S1.Pin_4, D4.anode
  N8: S2.Pin_3, S2.Pin_4, D3.anode
  N9: S3.Pin_3, S3.Pin_4, D7.anode
  N10: D3.cathode, D4.cathode, D7.cathode, XIAO_ESP32S3.D3
  N11: D5.cathode, D6.cathode, D8.cathode, XIAO_ESP32S3.D8
  VCC: R2.Pin_0, R3.Pin_0, Part1.VCC, XIAO_ESP32S3.3V3
  N12: R2.Pin_1, XIAO_ESP32S3.D6, RE1.EncoderPinB
  N13: R3.Pin_1, XIAO_ESP32S3.D7, RE1.EncoderPinA
  GND: Part1.GND, XIAO_ESP32S3.GND, RE1.EncoderPinC
  N14: Part1.HORZ, XIAO_ESP32S3.D10
  N15: Part1.VERT, XIAO_ESP32S3.D9

notes:
  GPIO7 (Input)
  GPIO4 (Input)
  GPIO6 (Output)
  GPIO5 (Output)
  GPIO3 (Output)
  GPIO44 (Input)
  GPIO43 (Input)
  GPIO8 (AnalogInput)
  GPIO9 (AnalogInput)
  ※ジョイスティック向き注意（KY-023 は逆）

custom parts:
  XIAO ESP32S3: Seeed Studio XIAO ESP32S3 leverages 240MHz Xtensa 32-bit LX7 dual-core processor, supporting both WiFi and BLE 5.0 wireless connectivities, a 2.4GHz Rod antenna, allows for deep sleep mode with power consumption as low as 14μA while supporting lithium battery charging management. Ideal for the Internet of Things, Smart Homes, Wireless wearable devices, Robotics, etc.
